# Fritzing sketch ESP32_alert (saved by Fritzing 0.9.6b)
breadboards: 2

parts:
  OLED1 = SSD1306 0.96in 128x64 I2C Monochrome OLED Display
  ESP1 = ESP32-DevkitC
  J1 = Piezo Speaker  # not connected

nets:
  GND: OLED1.GND, ESP1.GND
  VCC: OLED1.VCC, ESP1.3V3
  N1: OLED1.SCL, ESP1.IO22
  N2: OLED1.SDA, ESP1.IO21
